# Fritzing sketch RTC Bird Feeder (saved by Fritzing 0.9.3b)
breadboards: 3

parts:
  ZS-042_RTC1 = ZS-042 RTC Module
  LCD(20_4) = LCD screen
  Part1 = RobotDyn UNO R3 CH340
  S1 = Pushbutton [package="[THT]"]
  S2 = Pushbutton [package="[THT]"]
  S3 = Pushbutton [package="[SMD]"]
  S4 = Pushbutton [package="[SMD]"]
  U1 = POT [package=pot_mammoth]
  J1 = Basic Servo
  J2 = Basic Servo
  BAT1 = BC9VPC [package=bc9vpc]
  R1 = Resistor [tolerance=±5% resistance=220 package="1206 [SMD]"]
  R2 = Resistor [tolerance=±5% resistance=220 package="1206 [SMD]"]
  R3 = Resistor [tolerance=±5% resistance=220 package="1206 [SMD]"]
  R4 = Resistor [tolerance=±5% resistance=220 package="1206 [SMD]"]

nets:
  GND: ZS-042_RTC1.GND, LCD(20_4).VSS, LCD(20_4).LED+, Part1.GND, U1.E, J1.gnd, J2.gnd, BAT1.V-, R1.Pin_1, R2.Pin_1, R3.Pin_1, R4.Pin_1
  VCC: ZS-042_RTC1.VCC, LCD(20_4).VDD, LCD(20_4).LED-, Part1.5V, S1.Pin_3, S1.Pin_4, S2.Pin_3, S2.Pin_4, S3.Pin_3, S3.Pin_4, S4.Pin_3, S4.Pin_4
  N1: ZS-042_RTC1.SDA, Part1.A4/SDA
  N2: ZS-042_RTC1.SCL, Part1.A5/SCL
  N3: LCD(20_4).V0, U1.A
  N4: LCD(20_4).RS, Part1.D7
  N5: LCD(20_4).R/W, Part1.D6_PWM
  N6: LCD(20_4).DB4, Part1.D5_PWM
  N7: LCD(20_4).DB5, Part1.D4
  N8: LCD(20_4).DB6, Part1.D3_PWM
  N9: LCD(20_4).DB7, Part1.D2
  N10: Part1.A0, S1.Pin_1, S1.Pin_2
  N11: Part1.A1, S2.Pin_1, S2.Pin_2
  N12: Part1.A2, S3.Pin_1, S3.Pin_2
  N13: Part1.A3, S4.Pin_1, S4.Pin_2
  N14: Part1.D9_PWM, J1.pulse
  N15: Part1.D10_PWM/SS, J2.pulse
  VCC_2: J1.vcc, J2.vcc, BAT1.V+

notes:
  Connect a battery or a battery charger to power servos

custom parts:
  LCD screen: A standard character display, usually with 2x16 characters. Comes in many colors.
  RobotDyn UNO R3 CH340: Uno R3 CH340G/ATmega328P - compatible with the Arduino Uno R3 board, based on the microcontroller ATmega328P (SMD-version) and USB-UART interface chip CH340G.
